# Fritzing sketch circuit (saved by Fritzing 0.9.4)
circuit board: 4.06157cm x 5.67997cm
breadboards: 1

parts:
  J1 = female pin header, 5 pins [form="♀ (female)"]
  J2 = female pin header, 4 pins [form="♀ (female)"]
  J3 = female pin header, 2 pins [form="♀ (female)"]
  Part2 = Arduino Micro (Rev3)
  U3 = SUP500F [package=sup500f]
  J4 = female pin header, 4 pins [form="♀ (female)"]
  J5 = female pin header, 2 pins [form="♀ (female)"]

nets:
  N1: J1.pin1, J1.pin2, J2.pin4, J3.pin1, Part2.GND, J4.pin4, J5.pin1
  N2: J1.pin3, J2.pin1, Part2.A5
  N3: J1.pin4, J2.pin2, Part2.A4
  N4: J1.pin5, J2.pin3, Part2.5V, J4.pin1, J5.pin2
  N5: J3.pin2, Part2.A0
  N6: Part2.D2/SDA, U3.TX, J4.pin3
  N7: Part2.D3/SCL, U3.RX, J4.pin2

custom parts:
  SUP500F: SUP500F Venus GPS
